# Fritzing sketch Favero_repeater_v2_TEST_PCB (saved by Fritzing 1.0.1rc)
circuit board: 8.2cm x 4.2cm
perfboards: 1

parts:
  Screw_terminal = screw terminal, 4 pins
  FOTR = Resistor [tolerance=±5% resistance=33 package="1206 [SMD]"]
  FOTL = Resistor [tolerance=±5% resistance=33 package="1206 [SMD]"]
  RJ11 = RJ11 Jack [package=rj11-6]
  Serial_resistor1 = Resistor [tolerance=±5% resistance=100 package="1206 [SMD]"]
  Wemos = WeMos D1 Mini
  DC_5v_20a_Power_Supply = DC Power [voltage=5]

nets:
  GND: Screw_terminal.pin1, Serial_resistor1.Pin_0, Wemos.G
  N1: Screw_terminal.pin2, Wemos.5V, DC_5v_20a_Power_Supply.V-
  N2: Screw_terminal.pin3, FOTR.Pin_0
  N3: Screw_terminal.pin4, FOTL.Pin_0
  N4: FOTR.Pin_1, Wemos.D2
  N5: FOTL.Pin_1, Wemos.D1
  N6: RJ11.3, Serial_resistor1.Pin_1
  N7: RJ11.4, Wemos.RX
  N8: RJ11.5, Wemos.3V3

notes:
  Fencing_Repeater
  By Brad Riley
  +5v
  GND
